// Logisim project 7SegmentLEDcustom.circ as structural Verilog: 1 circuit, main circuit 7SegmentLED
module _7SegmentLED (
  input  I3,
  input  I2,
  input  I2_2,
  input  I0
);

  wire and_1_out, and_2_out, and_3_out, and_4_out, and_5_out, and_6_out, and_7_out, and_8_out, and_9_out,
       and_10_out, and_11_out, and_12_out, and_13_out, and_14_out, and_15_out, and_16_out, D0_out, D1_out,
       D2_out, D3_out, D4_out, D5_out, D6_out, not_1_out, not_2_out, not_3_out, not_4_out, not_5_out,
       not_6_out, not_7_out, not_8_out, not_9_out, not_10_out, not_11_out, not_12_out, not_13_out,
       not_14_out, not_15_out, not_16_out, not_17_out, not_18_out, not_19_out, not_20_out, not_21_out,
       not_22_out, not_23_out;

  not not_1 (not_1_out, I2);
  and and_1 (and_1_out, not_1_out, not_2_out);
  not not_2 (not_2_out, I0);
  not not_3 (not_3_out, I2);
  and and_2 (and_2_out, not_3_out, I2_2);
  and and_3 (and_3_out, I2_2, not_4_out);
  not not_4 (not_4_out, I0);
  and and_4 (and_4_out, I2, not_5_out, I0);
  not not_5 (not_5_out, I2_2);
  not not_6 (not_6_out, I2_2);
  not not_7 (not_7_out, I2);
  not not_8 (not_8_out, I2_2);
  and and_5 (and_5_out, not_7_out, not_8_out, not_9_out);
  not not_9 (not_9_out, I0);
  not not_10 (not_10_out, I3);
  and and_6 (and_6_out, not_10_out, I2_2, not_11_out);
  not not_11 (not_11_out, I0);
  not not_12 (not_12_out, I2);
  and and_7 (and_7_out, not_12_out, I2_2);
  and and_8 (and_8_out, I2, not_13_out);
  not not_13 (not_13_out, I2_2);
  and and_9 (and_9_out, I2, not_14_out);
  not not_14 (not_14_out, I0);
  not not_15 (not_15_out, I2);
  not not_16 (not_16_out, I2_2);
  and and_10 (and_10_out, not_16_out, not_17_out);
  not not_17 (not_17_out, I0);
  and and_11 (and_11_out, I2_2, I0);
  not not_18 (not_18_out, I2_2);
  and and_12 (and_12_out, not_18_out, not_19_out);
  not not_19 (not_19_out, I0);
  and and_13 (and_13_out, I2, not_20_out);
  not not_20 (not_20_out, I2_2);
  and and_14 (and_14_out, I2, not_21_out);
  not not_21 (not_21_out, I0);
  not not_22 (not_22_out, I2);
  and and_15 (and_15_out, not_22_out, not_23_out);
  not not_23 (not_23_out, I0);
  and and_16 (and_16_out, I2, I0);
  or D0 (D0_out, and_1_out, and_2_out, and_3_out, and_4_out, I3);
  or D1 (D1_out, not_6_out, I0, I2, I3);
  or D2 (D2_out, and_5_out, and_6_out);
  or D3 (D3_out, and_7_out, and_8_out, and_9_out, I3);
  or D4 (D4_out, not_15_out, and_10_out, and_11_out, I3);
  or D5 (D5_out, and_12_out, and_13_out, and_14_out, I3);
  or D6 (D6_out, and_15_out, I2_2, and_16_out, I3);
  _7_Segment_Display u_7_segment_display_1 (
    .g(D3_out), .f(D5_out), .a(D6_out), .b(D4_out), .e(D2_out), .d(D0_out), .c(D1_out));  // open: dp
endmodule
